// Logisim project cpu-circuit.circ as structural Verilog: 1 circuit, main circuit main
module main (
  input  in_1,
  input  in_2
);

  wire adder_1_cout, and_1_out, and_2_out, and_3_out, and_4_out, and_6_out, and_7_out, and_8_out, CARR_BIT,
       CARRY_FLAG, CLK, clock_1_out, controlled_buffer_18_out, controlled_buffer_19_out, COUNT_ENABLE,
       counter_1_carry, d_ff_1_q, DISP_REG_WRITE, DIV, EI, EO, EXP_READ, EXP_WRITE, FLAG_REG_WRITE, INV_CLK,
       JUMP, LOAD_ROM, MEM_READ, MEM_WRITE, MULT, n7_segment_display_1_p1, n7_segment_display_2_p1,
       n7_segment_display_3_p1, n7_segment_display_4_p1, n7_segment_display_5_p1, n7_segment_display_6_p1,
       n7_segment_display_7_p1, n7_segment_display_8_p1, n7_segment_display_9_p1, n7_segment_display_10_p1,
       n7_segment_display_11_p1, n7_segment_display_12_p1, not_1_out, not_3_out, not_4_out, not_5_out,
       not_6_out, not_7_out, not_8_out, not_9_out, not_10_out, or_1_out, or_2_out, PRG_CNT_READ, REG_A_READ,
       REG_A_WRITE, REG_B_READ, REG_B_WRITE, REG_C_READ, REG_C_WRITE, REG_INS_READ, REG_INS_WRITE,
       REG_MEMADDR_WRITE, ROM_LOAD_CLOCK, STOP, SUB, ZERO_FLAG;
  wire [1:0] controlled_buffer_22_out;
  wire [3:0] controlled_buffer_21_out, INSTR_STEP_COUNTER_q;
  wire [4:0] buffer_3_out, controlled_buffer_23_out, INS_DECODER;
  wire [5:0] rgb_video_1_p3, rgb_video_1_p4;
  wire [7:0] and_5_out, binary_to_bcd_converter_2_p1, buffer_10_out, counter_4_q;
  wire [7:2] register_1_q;
  wire [8:0] rom_1_data;
  wire [10:0] dipswitch_2_sw11, INSTR_REG_q;
  wire [11:0] controlled_buffer_16_out, counter_3_q;
  wire [15:0] adder_1_out, ALU_IN_A, ALU_IN_B, ALU_VALUE, buffer_2_out, C_REG_q, controlled_buffer_25_out,
       controlled_inverter_1_out, dipswitch_1_sw16, DISP_REG_q, divider_1_out, divider_1_rem,
       MEM_ADDRESS_REG_q, MEMORY_dout, multiplier_1_cout, multiplier_1_out, PROGRAM_ROM_data;

  Clock clock_1 (.out(clock_1_out));
  and and_1 (and_1_out, not_1_out, not_3_out);
  not not_1 (not_1_out, STOP);
  assign ROM_LOAD_CLOCK = LOAD_ROM ? clock_1_out : 1'bz;  // Controlled_Buffer controlled_buffer_1
  assign CLK = LOAD_ROM ? in_1 : 1'bz;  // Controlled_Buffer controlled_buffer_2
  assign CLK = and_1_out ? clock_1_out : 1'bz;  // Controlled_Buffer controlled_buffer_3
  not not_2 (INV_CLK, CLK);
  not not_3 (not_3_out, LOAD_ROM);
  // _7_Segment_Display 7_segment_display_1: pin names not known; wires that end beside it: n7_segment_display_1_p1, n7_segment_display_1_p1
  // BCD_to_7_Segment_decoder bcd_to_7_segment_decoder_1: pin names not known
  // Binary_to_BCD_converter #(.binvalue(8)) binary_to_bcd_converter_1: pin names not known
  // _7_Segment_Display 7_segment_display_2: pin names not known; wires that end beside it: n7_segment_display_2_p1, n7_segment_display_2_p1
  // BCD_to_7_Segment_decoder bcd_to_7_segment_decoder_2: pin names not known
  // _7_Segment_Display 7_segment_display_3: pin names not known; wires that end beside it: n7_segment_display_3_p1, n7_segment_display_3_p1
  // BCD_to_7_Segment_decoder bcd_to_7_segment_decoder_3: pin names not known
  Register #(.width(16)) A_Reg (.D(ALU_VALUE), .en(REG_A_WRITE), .clk(CLK), .Q(ALU_IN_A));  // open: clr
  Register #(.width(16)) B_REG (.D(ALU_VALUE), .en(REG_B_WRITE), .clk(CLK), .Q(ALU_IN_B));  // open: clr
  Register #(.width(16)) C_REG (.D(ALU_VALUE), .en(REG_C_WRITE), .clk(CLK), .Q(C_REG_q));  // open: clr
  // Buffer buffer_1 is placed but not wired
  LED led_1 (.in(binary_to_bcd_converter_2_p1[7]));
  LED led_2 (.in(binary_to_bcd_converter_2_p1[6]));
  LED led_3 (.in(binary_to_bcd_converter_2_p1[5]));
  LED led_4 (.in(binary_to_bcd_converter_2_p1[4]));
  // _7_Segment_Display 7_segment_display_4: pin names not known; wires that end beside it: n7_segment_display_4_p1, n7_segment_display_4_p1
  // _7_Segment_Display 7_segment_display_5: pin names not known; wires that end beside it: n7_segment_display_5_p1, n7_segment_display_5_p1
  // BCD_to_7_Segment_decoder bcd_to_7_segment_decoder_4: pin names not known
  // BCD_to_7_Segment_decoder bcd_to_7_segment_decoder_5: pin names not known
  // Binary_to_BCD_converter #(.binvalue(8)) binary_to_bcd_converter_2: pin names not known; wires that end beside it: binary_to_bcd_converter_2_p1
  assign ALU_VALUE = REG_A_READ ? ALU_IN_A : 16'bz;  // Controlled_Buffer controlled_buffer_4
  // Probe on ALU_IN_A
  assign ALU_VALUE = REG_B_READ ? ALU_IN_B : 16'bz;  // Controlled_Buffer controlled_buffer_5
  // Probe on ALU_IN_B
  assign ALU_VALUE = REG_C_READ ? C_REG_q : 16'bz;  // Controlled_Buffer controlled_buffer_6
  // Probe on C_REG_q
  LED led_5 (.in(binary_to_bcd_converter_2_p1[3]));
  LED led_6 (.in(binary_to_bcd_converter_2_p1[2]));
  LED led_7 (.in(binary_to_bcd_converter_2_p1[1]));
  LED led_8 (.in(binary_to_bcd_converter_2_p1[0]));
  // _7_Segment_Display 7_segment_display_6: pin names not known; wires that end beside it: n7_segment_display_6_p1, n7_segment_display_6_p1
  // BCD_to_7_Segment_decoder bcd_to_7_segment_decoder_6: pin names not known
  DipSwitch #(.number(16)) dipswitch_1 (
    .sw1(dipswitch_1_sw16[15]), .sw2(dipswitch_1_sw16[14]), .sw3(dipswitch_1_sw16[13]),
    .sw4(dipswitch_1_sw16[12]), .sw5(dipswitch_1_sw16[11]), .sw6(dipswitch_1_sw16[10]),
    .sw7(dipswitch_1_sw16[9]), .sw8(dipswitch_1_sw16[8]), .sw9(dipswitch_1_sw16[7]),
    .sw10(dipswitch_1_sw16[6]), .sw11(dipswitch_1_sw16[5]), .sw12(dipswitch_1_sw16[4]),
    .sw13(dipswitch_1_sw16[3]), .sw14(dipswitch_1_sw16[2]), .sw15(dipswitch_1_sw16[1]),
    .sw16(dipswitch_1_sw16[0]));
  // Probe on dipswitch_1_sw16
  not not_4 (not_4_out, EO);
  assign CARR_BIT = not_4_out ? 1'b0 : 1'bz;  // Controlled_Buffer controlled_buffer_7
  // _7_Segment_Display 7_segment_display_7: pin names not known; wires that end beside it: n7_segment_display_7_p1, n7_segment_display_7_p1
  // BCD_to_7_Segment_decoder bcd_to_7_segment_decoder_7: pin names not known
  // Binary_to_BCD_converter #(.binvalue(8)) binary_to_bcd_converter_3: pin names not known; wires that end beside it: dipswitch_1_sw16[15:8]
  // _7_Segment_Display 7_segment_display_8: pin names not known; wires that end beside it: n7_segment_display_8_p1, n7_segment_display_8_p1
  // _7_Segment_Display 7_segment_display_9: pin names not known; wires that end beside it: n7_segment_display_9_p1, n7_segment_display_9_p1
  // BCD_to_7_Segment_decoder bcd_to_7_segment_decoder_8: pin names not known
  // BCD_to_7_Segment_decoder bcd_to_7_segment_decoder_9: pin names not known
  // _7_Segment_Display 7_segment_display_10: pin names not known; wires that end beside it: n7_segment_display_10_p1, n7_segment_display_10_p1
  // BCD_to_7_Segment_decoder bcd_to_7_segment_decoder_10: pin names not known
  // Binary_to_BCD_converter #(.binvalue(8)) binary_to_bcd_converter_4: pin names not known; wires that end beside it: dipswitch_1_sw16[7:0]
  assign controlled_inverter_1_out = SUB ? ~ALU_IN_B : 16'bz;  // Controlled_Inverter controlled_inverter_1
  not not_5 (not_5_out, SUB);
  assign controlled_inverter_1_out = not_5_out ? ALU_IN_B : 16'bz;  // Controlled_Buffer controlled_buffer_8
  // _7_Segment_Display 7_segment_display_11: pin names not known; wires that end beside it: n7_segment_display_11_p1, n7_segment_display_11_p1
  // BCD_to_7_Segment_decoder bcd_to_7_segment_decoder_11: pin names not known
  or or_1 (or_1_out, multiplier_1_cout[15], multiplier_1_cout[14], multiplier_1_cout[13], multiplier_1_cout[12], multiplier_1_cout[11], multiplier_1_cout[10], multiplier_1_cout[9], multiplier_1_cout[8], multiplier_1_cout[7], multiplier_1_cout[6], multiplier_1_cout[5], multiplier_1_cout[4], multiplier_1_cout[3], multiplier_1_cout[2], multiplier_1_cout[1], multiplier_1_cout[0]);
  assign CARR_BIT = and_3_out ? or_1_out : 1'bz;  // Controlled_Buffer controlled_buffer_9
  or or_2 (or_2_out, divider_1_rem[15], divider_1_rem[14], divider_1_rem[13], divider_1_rem[12], divider_1_rem[11], divider_1_rem[10], divider_1_rem[9], divider_1_rem[8], divider_1_rem[7], divider_1_rem[6], divider_1_rem[5], divider_1_rem[4], divider_1_rem[3], divider_1_rem[2], divider_1_rem[1], divider_1_rem[0]);
  assign CARR_BIT = and_4_out ? or_2_out : 1'bz;  // Controlled_Buffer controlled_buffer_10
  // _7_Segment_Display 7_segment_display_12: pin names not known; wires that end beside it: n7_segment_display_12_p1, n7_segment_display_12_p1
  // BCD_to_7_Segment_decoder bcd_to_7_segment_decoder_12: pin names not known
  Adder #(.width(16)) adder_1 (
    .a(controlled_inverter_1_out), .b(ALU_IN_A), .out(adder_1_out), .cin(SUB), .cout(adder_1_cout));
  assign CARR_BIT = and_2_out ? adder_1_cout : 1'bz;  // Controlled_Buffer controlled_buffer_11
  Multiplier #(.width(16)) multiplier_1 (
    .a(ALU_IN_B), .b(ALU_IN_A), .out(multiplier_1_out), .cout(multiplier_1_cout));  // open: cin
  // Probe on divider_1_out
  Divider #(.width(16)) divider_1 (
    .a(ALU_IN_A), .b(ALU_IN_B), .out(divider_1_out), .rem(divider_1_rem));  // open: upper
  and and_2 (and_2_out, ~MULT, EO, ~DIV);  // AND_Gate
  assign ALU_VALUE = and_2_out ? adder_1_out : 16'bz;  // Controlled_Buffer controlled_buffer_12
  and and_3 (and_3_out, MULT, EO, ~DIV);  // AND_Gate
  assign ALU_VALUE = and_3_out ? multiplier_1_out : 16'bz;  // Controlled_Buffer controlled_buffer_13
  and and_4 (and_4_out, ~MULT, EO, DIV);  // AND_Gate
  assign ALU_VALUE = and_4_out ? divider_1_out : 16'bz;  // Controlled_Buffer controlled_buffer_14
  // Probe on ALU_VALUE
  Register #(.width(16)) DISP_REG (.D(ALU_VALUE), .en(DISP_REG_WRITE), .clk(CLK), .Q(DISP_REG_q));  // open: clr
  // Probe on DISP_REG_q
  // Probe on DISP_REG_q
  // RGB_Video #(.height(64), .scale(4), .width(64)) rgb_video_1: pin names not known; wires that end beside it: CLK, DISP_REG_WRITE, rgb_video_1_p3, rgb_video_1_p4, DISP_REG_q[14:0]
  // Shift_Register #(.length(2)) shift_register_1: pin names not known; wires that end beside it: 1'b1, DISP_REG_WRITE, DISP_REG_WRITE
  Register #(.width(16)) INSTR_REG (
    .D(ALU_VALUE), .en(REG_INS_WRITE), .clk(CLK), .Q({INS_DECODER, INSTR_REG_q}));  // open: clr
  assign buffer_2_out = ALU_VALUE;  // Buffer buffer_2, 16 bits wide
  // Probe on INSTR_REG_q
  // Probe on {INS_DECODER, INSTR_REG_q}
  and and_5 (and_5_out[0], ~buffer_2_out[0], ~buffer_2_out[1], ~buffer_2_out[2], ~buffer_2_out[3], ~buffer_2_out[4], ~buffer_2_out[5], ~buffer_2_out[6], ~buffer_2_out[7], ~buffer_2_out[8], ~buffer_2_out[9], ~buffer_2_out[10], ~buffer_2_out[11], ~buffer_2_out[12], ~buffer_2_out[13], ~buffer_2_out[14], ~buffer_2_out[15]);  // AND_Gate
  D_Flip_Flop d_ff_1 (.D(DISP_REG_WRITE), .clk(INV_CLK), .Q(d_ff_1_q));  // open: Qn, preset, reset
  not not_6 (not_6_out, REG_INS_WRITE);
  and and_6 (and_6_out, not_6_out, REG_INS_READ);
  assign buffer_3_out = {5{1'b0}};  // Buffer buffer_3, 5 bits wide
  // Probe on INS_DECODER
  buf buffer_4 (and_5_out[2], 1'b0);
  buf buffer_5 (and_5_out[3], 1'b0);
  buf buffer_6 (and_5_out[4], 1'b0);
  buf buffer_7 (and_5_out[5], 1'b0);
  Register register_1 (
    .D({and_5_out[7:2], CARR_BIT, and_5_out[0]}), .en(FLAG_REG_WRITE), .clk(CLK),
    .Q({register_1_q, CARRY_FLAG, ZERO_FLAG}));  // open: clr
  buf buffer_8 (and_5_out[6], 1'b0);
  buf buffer_9 (and_5_out[7], 1'b0);
  Counter #(.max('h3f), .width(6)) counter_1 (
    .clk(d_ff_1_q), .carry(counter_1_carry), .Q(rgb_video_1_p3));  // open: clr, load, up, count, D
  assign ALU_VALUE = and_6_out ? {buffer_3_out, INSTR_REG_q} : 16'bz;  // Controlled_Buffer controlled_buffer_15
  Counter #(.max('h3f), .width(6)) counter_2 (
    .clk(and_7_out), .Q(rgb_video_1_p4));  // open: clr, load, up, count, D, carry
  buf and_7 (and_7_out, ~counter_1_carry);  // AND_Gate AND_Gate
  Counter #(.max('hfff), .width(12)) counter_3 (
    .clk(ROM_LOAD_CLOCK), .Q(counter_3_q));  // open: clr, load, up, count, D, carry
  Counter #(.max('h9), .width(4)) INSTR_STEP_COUNTER (
    .clr(EI), .clk(INV_CLK), .Q(INSTR_STEP_COUNTER_q));  // open: load, up, count, D, carry
  Register #(.width(16)) MEM_ADDRESS_REG (
    .D(ALU_VALUE), .en(REG_MEMADDR_WRITE), .clk(CLK), .Q(MEM_ADDRESS_REG_q));  // open: clr
  // Probe on MEM_ADDRESS_REG_q[11:0]
  // Probe on MEM_ADDRESS_REG_q
  ROM #(.addrWidth(12), .dataWidth(16)) PROGRAM_ROM (.addr(counter_3_q), .data(PROGRAM_ROM_data));
  and and_8 (and_8_out, counter_3_q[0], counter_3_q[1], counter_3_q[2], counter_3_q[3], counter_3_q[4], counter_3_q[5], counter_3_q[6], counter_3_q[7], counter_3_q[8], counter_3_q[9], counter_3_q[10], counter_3_q[11]);
  Decoder #(.enable("false"), .select(4)) decoder_1 (.sel(INSTR_STEP_COUNTER_q));  // open: out0, out1, out2, out3, out4, out5, out6, out7, out8, out9, out10, out11, out12, out13, out14, out15
  DipSwitch #(.number(11)) dipswitch_2 (
    .sw1(dipswitch_2_sw11[10]), .sw2(dipswitch_2_sw11[9]), .sw3(dipswitch_2_sw11[8]),
    .sw4(dipswitch_2_sw11[7]), .sw5(dipswitch_2_sw11[6]), .sw6(dipswitch_2_sw11[5]),
    .sw7(dipswitch_2_sw11[4]), .sw8(dipswitch_2_sw11[3]), .sw9(dipswitch_2_sw11[2]),
    .sw10(dipswitch_2_sw11[1]), .sw11(dipswitch_2_sw11[0]));
  not not_7 (not_7_out, LOAD_ROM);
  assign controlled_buffer_16_out = not_7_out ? MEM_ADDRESS_REG_q[11:0] : 12'bz;  // Controlled_Buffer controlled_buffer_16
  assign controlled_buffer_16_out = LOAD_ROM ? counter_3_q : 12'bz;  // Controlled_Buffer controlled_buffer_17
  assign controlled_buffer_18_out = not_7_out ? MEM_WRITE : 1'bz;  // Controlled_Buffer controlled_buffer_18
  assign controlled_buffer_19_out = LOAD_ROM ? ROM_LOAD_CLOCK : 1'bz;  // Controlled_Buffer controlled_buffer_19
  assign controlled_buffer_19_out = not_7_out ? CLK : 1'bz;  // Controlled_Buffer controlled_buffer_20
  not not_8 (not_8_out, and_8_out);
  assign controlled_buffer_21_out = 1'b1 ? INSTR_STEP_COUNTER_q : 4'bz;  // Controlled_Buffer controlled_buffer_21
  assign controlled_buffer_22_out = 1'b1 ? {ZERO_FLAG, CARRY_FLAG} : 2'bz;  // Controlled_Buffer controlled_buffer_22
  assign controlled_buffer_23_out = 1'b1 ? INS_DECODER : 5'bz;  // Controlled_Buffer controlled_buffer_23
  not not_9 (not_9_out, 1'b1);
  assign controlled_buffer_18_out = LOAD_ROM ? LOAD_ROM : 1'bz;  // Controlled_Buffer controlled_buffer_24
  assign controlled_buffer_25_out = not_10_out ? ALU_VALUE : 16'bz;  // Controlled_Buffer controlled_buffer_25
  assign controlled_buffer_25_out = LOAD_ROM ? PROGRAM_ROM_data : 16'bz;  // Controlled_Buffer controlled_buffer_26
  not not_10 (not_10_out, LOAD_ROM);
  xor xor_1 (LOAD_ROM, not_8_out, in_2);
  // Probe on {controlled_buffer_23_out, controlled_buffer_21_out, controlled_buffer_22_out}
  ROM #(.addrWidth(11), .dataWidth(14)) rom_1 (
    .addr({controlled_buffer_23_out, controlled_buffer_21_out, controlled_buffer_22_out}),
    .data({EO, COUNT_ENABLE, STOP, EI, FLAG_REG_WRITE, rom_1_data}));
  assign {controlled_buffer_23_out, controlled_buffer_21_out, controlled_buffer_22_out} = not_9_out ? dipswitch_2_sw11 : 11'bz;  // Controlled_Buffer controlled_buffer_27
  RAM #(.addrWidth(12), .asyncread("true"), .dataWidth(16), .\type ("nonvolatile")) MEMORY (
    .addr(controlled_buffer_16_out), .we(controlled_buffer_18_out), .clk(controlled_buffer_19_out),
    .din(controlled_buffer_25_out), .dout(MEMORY_dout));  // open: oe
  // Probe on {EO, COUNT_ENABLE, STOP, EI, FLAG_REG_WRITE, rom_1_data}
  // Probe on rom_1_data[8:5]
  assign ALU_VALUE = MEM_READ ? MEMORY_dout : 16'bz;  // Controlled_Buffer controlled_buffer_28
  // Probe on MEMORY_dout
  Demultiplexer #(.select(2)) demultiplexer_1 (
    .out1(SUB), .out2(MULT), .out3(DIV), .in(1'b1), .sel(rom_1_data[1:0]));  // open: out0
  Demultiplexer #(.select(3)) demultiplexer_2 (
    .out1(REG_A_READ), .out2(REG_B_READ), .out3(REG_C_READ), .out4(MEM_READ), .out5(REG_INS_READ),
    .out6(PRG_CNT_READ), .out7(EXP_READ), .in(1'b1), .sel(rom_1_data[4:2]));  // open: out0
  // Probe on rom_1_data[4:2]
  Demultiplexer #(.select(4)) demultiplexer_3 (
    .out1(REG_A_WRITE), .out2(REG_B_WRITE), .out3(REG_C_WRITE), .out4(REG_INS_WRITE), .out5(DISP_REG_WRITE),
    .out6(MEM_WRITE), .out7(JUMP), .out8(REG_MEMADDR_WRITE), .out9(EXP_WRITE), .in(1'b1),
    .sel(rom_1_data[8:5]));  // open: out0, out10, out11, out12, out13, out14, out15
  Counter counter_4 (
    .load(JUMP), .count(COUNT_ENABLE), .clk(CLK), .D(ALU_VALUE[7:0]), .Q(counter_4_q));  // open: clr, up, carry
  assign buffer_10_out = {8{1'b0}};  // Buffer buffer_10, 8 bits wide
  // Probe on ALU_VALUE
  assign ALU_VALUE = PRG_CNT_READ ? {buffer_10_out, counter_4_q} : 16'bz;  // Controlled_Buffer controlled_buffer_29

  // Other names for the same wires on the sheet: BUS_1[15:0] = ALU_VALUE

  // Notes on the sheet:
  //   BUS VALUE
  //   DISPLAY / OUTPUT
  //   contents of PROGRAM_ROM (hex, n*v repeats v):
  //   200f 2803 6800 9800 9000
  //   contents of rom_1 (hex, n*v repeats v):
  //   4*118 4*1090 4*400 52*0 4*118 4*1090 4*114 4*30 4*400 44*0 4*118 4*1090 4*114 4*50 4*400 44*0 4*118
  //   4*1090 4*114 4*70 4*400 44*0 4*118 4*1090 4*34 4*400 48*0 4*118 4*1090 4*54 4*400 48*0 4*118 4*1090
  //   4*5c 4*400 48*0 4*118 4*1090 4*124 4*400 48*0 4*118 4*1090 4*114 4*c4 4*400 44*0 4*118 4*1090 4*114
  //   4*cc 4*400 44*0 4*118 4*1090 4*2220 4*400 48*0 4*118 4*1090 4*2221 4*400 48*0 4*118 4*1090 4*2222
  //   4*400 48*0 4*118 4*1090 4*2223 4*400 48*0 4*118 4*1090 4*f4 4*400 48*0 4*118 4*1090 400 400 f4 f4
  //   4*400 48*0 4*118 4*1090 400 f4 400 f4 4*400 48*0 4*118 4*1090 4*104 4*30 4*400 44*0 4*118 4*1090
  //   4*800 4*400 48*0 4*118 4*1090 4*a4 4*400
endmodule
